# Fritzing sketch Fenix PCB completo (saved by Fritzing 0.9.3b)
circuit board: 5.72981cm x 10.1752cm
breadboards: 1

parts:
  Componente10 = Arduino Mega ADK (Rev3)
  J1 = female pin header, 8 pins [form="♀ (female)"]
  J2 = female pin header, 8 pins [form="♀ (female)"]
  J3 = female pin header, 8 pins [form="♀ (female)"]
  J4 = female pin header, 8 pins [form="♀ (female)"]
  JP5 = Header 2 [package=molex-1x2_lock]
  JP6 = Header 6 [package=molex-1x6-ra_lock]
  JP7 = Header 4 [package=molex-1x4_lock]
  R5 = Resistor [tolerance=±5% resistance=2.2k package=THT]
  R6 = Resistor [tolerance=±5% resistance=1k package=THT]
  J5 = Camdenboss CTB0158-3 [part_number=CTB0158-3 package=THT]
  J6 = Camdenboss CTB0158-2 [part_number=CTB0158-2 package=THT]
  J8 = female pin header, 1 pin [form="♀ (female)"]
  J9 = female pin header, 1 pin [form="♀ (female)"]
  J10 = Camdenboss CTB0158-2 [part_number=CTB0158-2 package=THT]
  J11 = Camdenboss CTB0158-2 [part_number=CTB0158-2 package=THT]

nets (from the pcb view):
  N1: Componente10.A8, J5.pin3
  N2: Componente10.A12, JP5.2
  N3: Componente10.A0, J3.pin1
  N4: Componente10.A1, J3.pin2
  N5: Componente10.A2, J3.pin3
  N6: Componente10.A3, J3.pin4
  N7: Componente10.A4, J3.pin5
  N8: Componente10.A5, J3.pin6
  N9: Componente10.A6, J3.pin7
  N10: Componente10.A7, J3.pin8
  N11: Componente10.D21/SCL, JP7.1
  N12: Componente10.D20/SDA, JP7.2
  N13: Componente10.D19/RX1, JP6.4
  N14: Componente10.D18/TX1, R6.Pin_0
  N15: Componente10.AREF, J1.pin8
  N16: Componente10.GND, J1.pin7, J2.pin6, J2.pin7, JP5.1, JP6.3, JP7.3, R5.Pin_1, J5.pin1, J11.pin1
  N17: Componente10.D13_PWM, J1.pin6
  N18: Componente10.D12_PWM, J1.pin5
  N19: Componente10.D11_PWM, J1.pin4
  N20: Componente10.D10_PWM, J1.pin3
  N21: Componente10.D9_PWM, J1.pin2
  N22: Componente10.D8_PWM, J1.pin1
  N23: Componente10.IOREF#302, J2.pin1
  N24: Componente10.IOREF#303, Componente10.5V, J2.pin2, J2.pin5, JP6.2, JP7.4, J5.pin2, J11.pin2
  N25: Componente10.RESET, J2.pin3
  N26: Componente10.3V3, J2.pin4
  N27: Componente10.VIN, J2.pin8
  N28: Componente10.D0/RX0, J4.pin1, J10.pin2
  N29: Componente10.D1/TX0, J4.pin2, J10.pin1
  N30: Componente10.D2_PWM, J4.pin3
  N31: Componente10.D3_PWM, J4.pin4
  N32: Componente10.D4_PWM, J4.pin5
  N33: Componente10.D5_PWM, J4.pin6
  N34: Componente10.D6_PWM, J4.pin7
  N35: Componente10.D7_PWM, J4.pin8
  N36: Componente10.D34, JP6.1
  N37: Componente10.D44, JP6.6
  N38: JP6.5, R5.Pin_0, R6.Pin_1
  N39: J6.pin1, J9.pin1
  N40: J6.pin2, J8.pin1
