# Fritzing sketch Fenix definitivo (saved by Fritzing 0.9.3b)
circuit board: 10.1776cm x 5.36194cm
breadboards: 1

parts:
  J2-Feedback = Camdenboss CTB0158-3 [part_number=CTB0158-3 package=THT]
  J3-Serial2 = Camdenboss CTB0158-3 [part_number=CTB0158-3 package=THT]
  JP3-BT = Header 6 [package=molex-1x6_lock]
  JP6-Eng_Control = Header 3 [package=molex-1x3_lock]
  JP5-S0 = Header 3 [package=molex-1x3_lock]
  JP4-I2C_IMU = Header 6 [package=molex-1x6_lock]
  JP2-Keypad = Header 2 [package=molex-1x2_lock]
  R1 = Resistor [tolerance=±5% resistance=1k package=THT]
  R2 = Resistor [tolerance=±5% resistance=2.2k package=THT]
  Buzzer = Buzzer 12mm [package=buzzer-12mm]
  Part1 = Arduino Mega Fenix Shield [part_number="Arduino Mega"]
  JP1-Buzzer = Header 2 [package=molex-1x2_lock]
  J1-Power_IN = Camdenboss CTB0158-2 [part_number=CTB0158-2 package=THT]

nets:
  GND: J2-Feedback.pin1, J3-Serial2.pin1, JP3-BT.3, JP6-Eng_Control.1, JP5-S0.1, JP4-I2C_IMU.2, JP4-I2C_IMU.5, JP2-Keypad.1, R2.Pin_1, Buzzer.1, Part1.GND, JP1-Buzzer.1, J1-Power_IN.pin1
  FEEDBACK: J2-Feedback.pin2, Part1.A8
  5V: J2-Feedback.pin3, JP3-BT.2, JP4-I2C_IMU.1, Part1.5V
  RX2: J3-Serial2.pin2, Part1.D17
  TX2: J3-Serial2.pin3, Part1.D16
  BT-KEY: JP3-BT.1, Part1.D34
  BT-RX1: JP3-BT.4, Part1.D19
  BT-TX1 3.3V: JP3-BT.5, R1.Pin_1, R2.Pin_0
  BT-STATE: JP3-BT.6, Part1.D44
  DIR: JP6-Eng_Control.2, Part1.D12
  PWM: JP6-Eng_Control.3, Part1.D11
  TX0: JP5-S0.2, Part1.TX1
  RX0: JP5-S0.3, Part1.RX0
  ATX/SDA: JP4-I2C_IMU.3, Part1.SDA
  LRX/SCK: JP4-I2C_IMU.4, Part1.SCL
  KEYPAD: JP2-Keypad.2, Part1.A0
  BT-TX1: R1.Pin_0, Part1.D18
  BUZZER: Buzzer.2, Part1.A12, JP1-Buzzer.2
  Vin: Part1.VIN, J1-Power_IN.pin2

notes:
  5V FBK GND
  TX2 RX2 GND
  Vin GND
  Fenix Megashield
  5 G SDSC G x
  K 5 G T1R1 S
  G T0R0
